// Logisim project Proj4.circ as structural Verilog: 2 circuits, main circuit divison
module divison (
  input  [15:0] Dividend,
  input  [15:0] Divisor,
  input  Initialize,
  output [15:0] Remainder,
  output [15:0] Quotient
);

  wire and_1_out, and_2_out, clock_1_out, counter_1_carry, not_1_out, not_2_out, or_1_out, subtractor_1_bout;
  wire [0:0] not_3_out;
  wire [4:0] counter_1_q;
  wire [15:0] adder_1_out, multiplexer_4_out, shifter_2_out;
  wire [31:0] multiplexer_1_out, multiplexer_2_out, multiplexer_3_out, register_2_q, shifter_1_out,
       subtractor_1_out;
  wire [31:16] register_1_q;

  not not_1 (not_1_out, Initialize);
  Clock clock_1 (.out(clock_1_out));
  Multiplexer #(.width(32), .enable("false")) multiplexer_1 (
    .in0({{16{1'b0}}, Dividend}), .in1(multiplexer_3_out), .out(multiplexer_1_out), .sel(or_1_out));
  Counter #(.width(5), .max('h12), .ongoal("stay"), .trigger("falling")) counter_1 (
    .Q(counter_1_q), .carry(counter_1_carry), .clk(and_1_out), .clr(not_1_out));  // open: load, D, count
  and and_1 (and_1_out, Initialize, clock_1_out);
  Register #(.width(32), .trigger("falling")) register_1 (
    .D(multiplexer_1_out), .Q({register_1_q, Remainder}), .clk(and_2_out));  // open: en, clr
  Multiplexer #(.width(32), .enable("false")) multiplexer_2 (
    .in0({Divisor, {16{1'b0}}}), .in1(shifter_1_out), .out(multiplexer_2_out), .sel(or_1_out));
  not not_2 (not_2_out, counter_1_carry);
  Register #(.width(32), .trigger("falling")) register_2 (
    .D(multiplexer_2_out), .Q(register_2_q), .clk(and_2_out));  // open: en, clr
  or or_1 (or_1_out, counter_1_q[0], counter_1_q[1], counter_1_q[2], counter_1_q[3], counter_1_q[4]);
  Subtractor #(.width(32)) subtractor_1 (
    .a({register_1_q, Remainder}), .b(register_2_q), .out(subtractor_1_out), .bout(subtractor_1_bout));  // open: bin
  Shifter #(.width(32), .shift("lr")) shifter_1 (.in(register_2_q), .\dist (5'b00001), .out(shifter_1_out));
  and and_2 (and_2_out, not_2_out, and_1_out);
  Multiplexer #(.width(32), .enable("false")) multiplexer_3 (
    .in0(subtractor_1_out), .in1({register_1_q, Remainder}), .out(multiplexer_3_out), .sel(subtractor_1_bout));
  not not_3 (not_3_out[0], subtractor_1_bout);
  Shifter #(.width(16)) shifter_2 (.in(Quotient), .\dist (4'b0001), .out(shifter_2_out));
  Adder #(.width(16)) adder_1 (
    .a(shifter_2_out), .b({{15{1'b0}}, not_3_out[0]}), .out(adder_1_out));  // open: cin, cout
  Multiplexer #(.width(16), .enable("false")) multiplexer_4 (
    .in0({16{1'b0}}), .in1(adder_1_out), .out(multiplexer_4_out), .sel(or_1_out));
  Register #(.width(16), .trigger("falling")) register_3 (
    .D(multiplexer_4_out), .Q(Quotient), .clk(and_2_out));  // open: en, clr
endmodule

module Square_root (
  input  [7:0] Number,
  output [3:0] Result
);

  wire comparator_1_lt, comparator_2_lt, comparator_3_lt, comparator_4_lt;
  wire [0:0] multiplexer_1_out, multiplexer_2_out_2;
  wire [1:0] multiplexer_5_out, subtractor_2_out;
  wire [2:0] multiplexer_1_out_2;
  wire [3:0] adder_1_out, multiplexer_4_out, subtractor_1_out;
  wire [4:0] multiplexer_2_out;
  wire [5:0] adder_2_out, multiplexer_6_out, subtractor_3_out;
  wire [7:0] multiplexer_3_out;

  Multiplexer #(.width(4), .enable("false")) multiplexer_1 (
    .in0(4'b0001), .in1(4'b0101), .out({multiplexer_1_out_2, multiplexer_1_out[0]}), .sel(Result[3]));
  Adder #(.width(4)) adder_1 (
    .a({multiplexer_1_out_2, multiplexer_1_out[0]}), .b(4'b0001), .out(adder_1_out));  // open: cin, cout
  Adder #(.width(6)) adder_2 (
    .a({multiplexer_2_out, multiplexer_2_out_2[0]}), .b(6'b000001), .out(adder_2_out));  // open: cin, cout
  Multiplexer #(.width(6), .enable("false")) multiplexer_2 (
    .in0({1'b0, multiplexer_1_out_2, 2'b01}), .in1({1'b0, adder_1_out, 1'b1}),
    .out({multiplexer_2_out, multiplexer_2_out_2[0]}), .sel(Result[2]));
  Multiplexer #(.width(8), .enable("false")) multiplexer_3 (
    .in0({1'b0, multiplexer_2_out, 2'b01}), .in1({1'b0, adder_2_out, 1'b1}), .out(multiplexer_3_out),
    .sel(Result[1]));
  Subtractor #(.width(4)) subtractor_1 (
    .a({multiplexer_5_out, Number[5:4]}), .b({multiplexer_1_out_2, multiplexer_1_out[0]}),
    .out(subtractor_1_out));  // open: bin, bout
  Comparator #(.width(2)) comparator_1 (.a(Number[7:6]), .b(2'b01), .lt(comparator_1_lt));  // open: gt, eq
  Subtractor #(.width(2)) subtractor_2 (.a(Number[7:6]), .b(2'b01), .out(subtractor_2_out));  // open: bin, bout
  Comparator #(.width(4)) comparator_2 (
    .a({multiplexer_5_out, Number[5:4]}), .b({multiplexer_1_out_2, multiplexer_1_out[0]}),
    .lt(comparator_2_lt));  // open: gt, eq
  not not_1 (Result[2], comparator_2_lt);
  Multiplexer #(.width(4), .enable("false")) multiplexer_4 (
    .in0({multiplexer_5_out, Number[5:4]}), .in1(subtractor_1_out), .out(multiplexer_4_out), .sel(Result[2]));
  Comparator #(.width(6)) comparator_3 (
    .a({multiplexer_4_out, Number[3:2]}), .b({multiplexer_2_out, multiplexer_2_out_2[0]}),
    .lt(comparator_3_lt));  // open: gt, eq
  Subtractor #(.width(6)) subtractor_3 (
    .a({multiplexer_4_out, Number[3:2]}), .b({multiplexer_2_out, multiplexer_2_out_2[0]}),
    .out(subtractor_3_out));  // open: bin, bout
  Comparator comparator_4 (
    .a({multiplexer_6_out, Number[1:0]}), .b(multiplexer_3_out), .lt(comparator_4_lt));  // open: gt, eq
  not not_2 (Result[3], comparator_1_lt);
  Multiplexer #(.width(2), .enable("false")) multiplexer_5 (
    .in0(Number[7:6]), .in1(subtractor_2_out), .out(multiplexer_5_out), .sel(Result[3]));
  not not_3 (Result[1], comparator_3_lt);
  Multiplexer #(.width(6), .enable("false")) multiplexer_6 (
    .in0({multiplexer_4_out, Number[3:2]}), .in1(subtractor_3_out), .out(multiplexer_6_out), .sel(Result[1]));
  not not_4 (Result[0], comparator_4_lt);
endmodule
